# Fritzing sketch oiltempjan (saved by Fritzing 1.0.2b)
breadboards: 1

parts:
  A2 = Arduino Nano ESP32
  Bauteil1 = Adafruit ADS1115 16Bit I2C ADC [part_number="Adafruit #1085"]
  LCD1 = Waveshare 1.28 inch Round 240x240 LCD Display
  R1 = Temperature Sensor (Thermistor) [thermistor_type=NTC package=THT]
  R2 = Resistor [tolerance=±5% resistance=10k package="0805 [SMD]"]

nets:
  N1: A2.Pin_1, LCD1.pin4
  N2: A2.Pin_2, Bauteil1.AIN1, Bauteil1.VDD, LCD1.pin_1, R2.Pin_0
  N3: A2.Pin_6, Bauteil1.SDA
  N4: A2.Pin_7, Bauteil1.SCL
  N5: A2.Pin_14, A2.Pin_19, Bauteil1.GND, LCD1.pin2, R1.pin_0
  N6: A2.Pin_24, LCD1.pin_8
  N7: A2.Pin_25, LCD1.pin_7
  N8: A2.Pin_26, LCD1.pin_6
  N9: A2.Pin_27, LCD1.pin_5
  N10: A2.Pin_29, LCD1.pin3
  N11: Bauteil1.AIN0, R1.pin_1, R2.Pin_1

custom parts:
  Arduino Nano ESP32: Arduino® Nano ESP32 tht.
  Adafruit ADS1115 16Bit I2C ADC: For microcontrollers without an analog-to-digital converter or when you want a higher-precision ADC, the ADS1115 provides 16-bit precision at 860 samples/second over I2C. The chip can be configured as 4 single-ended input channels, or two differential channels. As a nice bonus, it even includes a programmable gain amplifier, up to x16, to help boost up smaller single/differential signals to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
  Waveshare 1.28 inch Round 240x240 LCD Display: Waveshare 1.28 inch Round 240x240 LCD Display with GC9A01 Controller
